# Fritzing sketch battery-monitor-sketch (saved by Fritzing 0.9.3b)

parts:
  U1 = NodeMCU V3.0
  R1 = Resistor [tolerance=±5% resistance=10k package="0805 [SMD]"]
  VCC1 = Battery
  R2 = Resistor [tolerance=±5% resistance=3k package="0805 [SMD]"]

nets:
  N1: U1.GND, R1.Pin_1, VCC1.+
  N2: U1.A0, R1.Pin_0, R2.Pin_0
  N3: VCC1.-, R2.Pin_1

custom parts:
  NodeMCU V3.0: ESP8266 based NodeMCU
  Battery: Your standard 2x 18650 battery pack (7,4 Volts)
