# Fritzing sketch rest_button_circuit (saved by Fritzing 0.9.3b)

parts:
  S1 = Momentary Switch [package=ksa_sealed_tac_switch]
  WeMos_D1_Mini1 = WeMos D1 Mini
  R2 = Resistor [tolerance=±5% resistance=1k package="0402 [SMD]"]
  S2 = Momentary Switch [package=ksa_sealed_tac_switch]
  R3 = Resistor [tolerance=±5% resistance=1k package="0402 [SMD]"]

nets:
  N1: S1.2, WeMos_D1_Mini1.D1, R2.Pin_1
  N2: S1.4, WeMos_D1_Mini1.3V3, S2.4
  N3: WeMos_D1_Mini1.D2, S2.2, R3.Pin_1
  N4: WeMos_D1_Mini1.G, R2.Pin_0, R3.Pin_0
