# Fritzing sketch esp8266-led-controller-rest-circuit (saved by Fritzing 0.9.3b)

parts:
  WeMos_D1_Mini1 = WeMos D1 Mini
  LED1 = LED - 5mm [color="White (4500K)" package="5 mm [THT]"]
  LED2 = LED - 5mm [color="White (4500K)" package="5 mm [THT]"]
  LED3 = LED - 5mm [color="White (4500K)" package="5 mm [THT]"]
  LED4 = LED - 5mm [color="White (4500K)" package="5 mm [THT]"]
  LED5 = LED - 5mm [color="White (4500K)" package="5 mm [THT]"]
  LED6 = LED - 5mm [color="White (4500K)" package="5 mm [THT]"]
  LED7 = LED - 5mm [color="White (4500K)" package="5 mm [THT]"]
  LED8 = LED - 5mm [color="White (4500K)" package="5 mm [THT]"]
  LED9 = LED - 5mm [color="White (4500K)" package="5 mm [THT]"]
  LED10 = LED - 5mm [color="White (4500K)" package="5 mm [THT]"]
  LED11 = LED - 5mm [color="White (4500K)" package="5 mm [THT]"]
  LED12 = LED - 5mm [color="White (4500K)" package="5 mm [THT]"]

nets:
  N1: WeMos_D1_Mini1.D1, LED9.anode, LED10.anode, LED11.anode, LED12.anode
  N2: WeMos_D1_Mini1.D2, LED5.anode, LED6.anode, LED7.anode, LED8.anode
  N3: WeMos_D1_Mini1.D3, LED1.anode, LED2.anode, LED3.anode, LED4.anode
  N4: WeMos_D1_Mini1.G, LED1.cathode, LED2.cathode, LED3.cathode, LED4.cathode, LED5.cathode, LED6.cathode, LED7.cathode, LED8.cathode, LED9.cathode, LED10.cathode, LED11.cathode, LED12.cathode
